// Logisim project proj_3.circ as structural Verilog: 1 circuit, main circuit main
module main (
  input  x
);

  _7_Segment_Display u_7_segment_display_1 ();  // open: g, f, a, b, e, d, c, dp
  _7_Segment_Display u_7_segment_display_2 ();  // open: g, f, a, b, e, d, c, dp
endmodule
